# Fritzing sketch laserpianoschematic (saved by Fritzing 0.9.3b)
breadboards: 1

parts:
  R1 = Resistor [tolerance=±5% resistance=10k package=THT]
  R2 = Resistor [tolerance=±5% resistance=10k package=THT]
  R3 = Resistor [tolerance=±5% resistance=10k package=THT]
  R4 = Resistor [tolerance=±5% resistance=10k package=THT]
  R5 = Resistor [tolerance=±5% resistance=10k package=THT]
  R6 = Resistor [tolerance=±5% resistance=10k package=THT]
  R7 = Photocell (LDR) [package=THT]
  R8 = Photocell (LDR) [package=THT]
  R9 = Photocell (LDR) [package=THT]
  R10 = Photocell (LDR) [package=THT]
  R11 = Photocell (LDR) [package=THT]
  R12 = Photocell (LDR) [package=THT]
  U1 = atmega328 [package=dip]
  C1 = Ceramic Capacitor [capacitance=100nF package="100 mil [THT, multilayer]"]
  R14 = Resistor [tolerance=±5% resistance=10k package=THT]
  SPKR1 = Loudspeaker
  S1 = Pushbutton [package="[THT]"]
  R15 = Resistor [tolerance=±5% resistance=10k package=THT]
  C2 = Ceramic Capacitor [capacitance=100nF package="100 mil [THT, multilayer]"]

nets:
  N1: R1.Pin_0, R10.pin_0, U1.A2
  N2: R1.Pin_1, R2.Pin_1, R3.Pin_1, R4.Pin_1, R5.Pin_1, R6.Pin_1, U1.RESET, U1.GND, C1.0, R14.Pin_0, R14.Pin_1, SPKR1.pin1, R15.Pin_0, C2.1
  N3: R2.Pin_0, R9.pin_1, U1.A3
  N4: R3.Pin_0, R11.pin_0, U1.A1
  N5: R4.Pin_0, R7.pin_1, U1.A5
  N6: R5.Pin_0, R12.pin_0, U1.A0
  N7: R6.Pin_0, R8.pin_1, U1.A4
  N8: R7.pin_0, R8.pin_0, R9.pin_0, R10.pin_1, R11.pin_1, R12.pin_1, U1.VCC, U1.AVCC, C1.1, S1.Pin_1, S1.Pin_2, C2.0
  N9: U1.D0_(RX), S1.Pin_3, S1.Pin_4, R15.Pin_1
  N10: U1.D9_(PWM), SPKR1.pin2
